// Logisim project proj_2_1.circ as structural Verilog: 7 circuits, main circuit testbench
module inst_fetch (
  input  clk,
  input  rst,
  input  control_en_i,
  input  [31:0] control_pc_i,
  input  [15:0] inst_i,
  output inst_en_o,
  output [31:0] current_pc_o,
  output [31:0] inst_addr_o,
  output [15:0] inst_o
);

  wire not_1_out, not_2_out;
  wire [31:0] adder_1_out, counter_1_q, multiplexer_1_out;

  not not_1 (not_1_out, rst);
  Adder #(.width(32)) adder_1 (.a(control_pc_i), .b(32'h1), .out(adder_1_out));  // open: cin, cout
  Counter #(.max('hffffffff), .width(32)) counter_1 (
    .clr(rst), .load(control_en_i), .up(not_1_out), .count(not_1_out), .clk(clk), .D(adder_1_out),
    .Q(counter_1_q));  // open: carry
  Multiplexer #(.width(32)) multiplexer_1 (
    .in0(counter_1_q), .in1(control_pc_i), .out(multiplexer_1_out), .sel(control_en_i));
  not not_2 (not_2_out, rst);
  Register #(.width(32)) register_1 (.D(multiplexer_1_out), .en(not_2_out), .clk(clk), .Q(current_pc_o), .clr(rst));
  not not_3 (inst_en_o, rst);

  assign inst_addr_o = current_pc_o;
  assign inst_o = inst_i;

  // Notes on the sheet:
  //   Don't touch
endmodule

module TOP (
  input  rst,
  input  clk,
  input  [15:0] inst,
  input  [31:0] mem_result,
  input  [31:0] current_pc,
  output mem_wen,
  output [31:0] mem_din,
  output mem_ren,
  output [31:0] alu_result,
  output control_en,
  output [31:0] control_pc,
  output wb_en,
  output [4:0] wb_addr,
  output [31:0] wb_data
);

  wire comparator_1_eq, or_1_out, rs2_or_imm_1_data_2_choose;
  wire [31:0] alu_file_1_alu_result, imm_gen_1_imm, multiplexer_1_out, register_file_1_read_data_1,
       register_file_1_read_data_2;

  register_file register_file_1 (
    .read_register_1(inst[11:7]), .read_register_2(inst[6:2]), .data_in(alu_file_1_alu_result),
    .write_enable(1'b1), .write_register(inst[11:7]), .clk(clk), .rst(rst),
    .read_data_1(register_file_1_read_data_1), .read_data_2(register_file_1_read_data_2));
  rs2_or_imm rs2_or_imm_1 (.inst(inst), .data_2_choose(rs2_or_imm_1_data_2_choose));
  imm_gen imm_gen_1 (.inst(inst), .imm(imm_gen_1_imm));
  Multiplexer #(.width(32)) multiplexer_1 (
    .in0(register_file_1_read_data_2), .in1(imm_gen_1_imm), .out(multiplexer_1_out),
    .sel(rs2_or_imm_1_data_2_choose));
  Comparator #(.width(16)) comparator_1 (.a(inst), .b(16'h1f40), .eq(comparator_1_eq));  // open: gt, lt
  alu_file alu_file_1 (
    .data_1(register_file_1_read_data_1), .data_2(multiplexer_1_out), .inst(inst),
    .alu_result(alu_file_1_alu_result));
  Multiplexer multiplexer_2 (.in0(1'b1), .in1(1'b0), .out(wb_en), .sel(or_1_out));
  or or_1 (or_1_out, comparator_1_eq, rst);
  Multiplexer #(.width(5)) multiplexer_3 (.in0(inst[11:7]), .in1({5{1'b0}}), .out(wb_addr), .sel(or_1_out));
  Multiplexer #(.width(32)) multiplexer_4 (
    .in0(alu_file_1_alu_result), .in1({32{1'b0}}), .out(wb_data), .sel(or_1_out));

  assign alu_result = {32{1'b0}};
  assign control_en = 1'b0;
  assign control_pc = {32{1'b0}};
  assign mem_din = {32{1'b0}};
  assign mem_ren = 1'b0;
  assign mem_wen = 1'b0;

  // Notes on the sheet:
  //   Fixed I/O
  //   rs2/imm
  //   rd/rs1
  //   Don't touch
endmodule

module testbench (
  input  rst,
  output mem_wen,
  output [31:0] mem_din,
  output mem_ren,
  output [31:0] alu_result,
  output control_en,
  output [31:0] control_pc,
  output halt,
  output wb_en,
  output [4:0] wb_addr,
  output [31:0] wb_data
);

  wire clk, inst_en, not_1_out, not_2_out, not_3_out, not_4_out, por_1_out, rst_t;
  wire [15:0] inst, inst_i;
  wire [31:0] current_pc, inst_addr, mem_result;

  not not_1 (not_1_out, inst_i[0]);
  not not_2 (not_2_out, inst_i[1]);
  not not_3 (not_3_out, inst_i[13]);
  not not_4 (not_4_out, inst_i[14]);
  and and_1 (halt, not_1_out, not_2_out, not_3_out, not_4_out, inst_i[15]);
  Clock clock_1 (.out(clk));
  or or_1 (rst_t, rst, por_1_out);
  POR por_1 (.out(por_1_out));
  inst_fetch inst_fetch_1 (
    .clk(clk), .rst(rst_t), .control_en_i(control_en), .control_pc_i(control_pc), .inst_i(inst_i),
    .inst_en_o(inst_en), .current_pc_o(current_pc), .inst_addr_o(inst_addr), .inst_o(inst));
  TOP top_1 (
    .rst(rst_t), .clk(clk), .inst(inst), .mem_result(mem_result), .current_pc(current_pc), .mem_wen(mem_wen),
    .mem_din(mem_din), .mem_ren(mem_ren), .alu_result(alu_result), .control_en(control_en),
    .control_pc(control_pc), .wb_en(wb_en), .wb_addr(wb_addr), .wb_data(wb_data));
  ROM #(.dataWidth(16)) rom_1 (.addr(inst_addr[7:0]), .data(inst_i));
  RAM #(.addrWidth(16), .clearpin("true"), .dataWidth(32), .\type ("nonvolatile")) ram_1 (
    .addr(alu_result[15:0]), .we(mem_wen), .oe(mem_ren), .clk(clk), .din(mem_din), .dout(mem_result),
    .clr(rst_t));

  // Notes on the sheet:
  //   contents of rom_1 (hex, n*v repeats v):
  //   4425 6525 40e 942a 84a2 49d 8000 1 1
  //   you can write any instruction in
endmodule

module register_file (
  input  [4:0] read_register_1,
  input  [4:0] read_register_2,
  input  [31:0] data_in,
  input  write_enable,
  input  [4:0] write_register,
  input  clk,
  input  rst,
  output [31:0] read_data_1,
  output [31:0] read_data_2
);

  wire demultiplexer_1_out0, demultiplexer_1_out2, demultiplexer_1_out8, demultiplexer_1_out9,
       demultiplexer_1_out10, demultiplexer_1_out11, demultiplexer_1_out12, demultiplexer_1_out13,
       demultiplexer_1_out14, demultiplexer_1_out15;
  wire [31:0] and_1_out, and_2_out, and_3_out, and_4_out, and_5_out, and_6_out, and_7_out, and_8_out,
       and_9_out, and_10_out, bit_extender_1_out, bit_extender_2_out, bit_extender_3_out, bit_extender_4_out,
       bit_extender_5_out, bit_extender_6_out, bit_extender_7_out, bit_extender_8_out, bit_extender_9_out,
       bit_extender_10_out, x0_q, x2_q, x8_q, x9_q, x10_q, x11_q, x12_q, x13_q, x14_q, x15_q;

  Demultiplexer #(.select(5)) demultiplexer_1 (
    .out0(demultiplexer_1_out0), .out2(demultiplexer_1_out2), .out8(demultiplexer_1_out8),
    .out9(demultiplexer_1_out9), .out10(demultiplexer_1_out10), .out11(demultiplexer_1_out11),
    .out12(demultiplexer_1_out12), .out13(demultiplexer_1_out13), .out14(demultiplexer_1_out14),
    .out15(demultiplexer_1_out15), .in(write_enable), .sel(write_register));  // open: out1, out3, out4, out5, out6, out7, out16, out17, out18, out19, out20, out21, out22, out23, out24, out25, out26, out27, out28, out29, out30, out31
  assign bit_extender_1_out = {{31{demultiplexer_1_out0}}, demultiplexer_1_out0};  // Bit_Extender bit_extender_1
  assign bit_extender_2_out = {{31{demultiplexer_1_out2}}, demultiplexer_1_out2};  // Bit_Extender bit_extender_2
  assign bit_extender_3_out = {{31{demultiplexer_1_out8}}, demultiplexer_1_out8};  // Bit_Extender bit_extender_3
  assign bit_extender_4_out = {{31{demultiplexer_1_out9}}, demultiplexer_1_out9};  // Bit_Extender bit_extender_4
  assign bit_extender_5_out = {{31{demultiplexer_1_out10}}, demultiplexer_1_out10};  // Bit_Extender bit_extender_5
  assign bit_extender_6_out = {{31{demultiplexer_1_out11}}, demultiplexer_1_out11};  // Bit_Extender bit_extender_6
  assign bit_extender_7_out = {{31{demultiplexer_1_out12}}, demultiplexer_1_out12};  // Bit_Extender bit_extender_7
  assign bit_extender_8_out = {{31{demultiplexer_1_out13}}, demultiplexer_1_out13};  // Bit_Extender bit_extender_8
  assign bit_extender_9_out = {{31{demultiplexer_1_out14}}, demultiplexer_1_out14};  // Bit_Extender bit_extender_9
  assign bit_extender_10_out = {{31{demultiplexer_1_out15}}, demultiplexer_1_out15};  // Bit_Extender bit_extender_10
  assign and_1_out = data_in & bit_extender_1_out;  // AND_Gate and_1, 32 bits wide
  assign and_2_out = data_in & bit_extender_2_out;  // AND_Gate and_2, 32 bits wide
  assign and_3_out = data_in & bit_extender_3_out;  // AND_Gate and_3, 32 bits wide
  assign and_4_out = data_in & bit_extender_4_out;  // AND_Gate and_4, 32 bits wide
  assign and_5_out = data_in & bit_extender_5_out;  // AND_Gate and_5, 32 bits wide
  assign and_6_out = data_in & bit_extender_6_out;  // AND_Gate and_6, 32 bits wide
  assign and_7_out = data_in & bit_extender_7_out;  // AND_Gate and_7, 32 bits wide
  assign and_8_out = data_in & bit_extender_8_out;  // AND_Gate and_8, 32 bits wide
  assign and_9_out = data_in & bit_extender_9_out;  // AND_Gate and_9, 32 bits wide
  assign and_10_out = data_in & bit_extender_10_out;  // AND_Gate and_10, 32 bits wide
  Register #(.width(32)) x0 (.D(and_1_out), .clk(clk), .Q(x0_q), .clr(rst));  // open: en
  Register #(.width(32)) x2 (.D(and_2_out), .clk(clk), .Q(x2_q), .clr(rst));  // open: en
  Register #(.width(32)) x8 (.D(and_3_out), .clk(clk), .Q(x8_q), .clr(rst));  // open: en
  Register #(.width(32)) x9 (.D(and_4_out), .clk(clk), .Q(x9_q), .clr(rst));  // open: en
  Register #(.width(32)) x10 (.D(and_5_out), .clk(clk), .Q(x10_q), .clr(rst));  // open: en
  Register #(.width(32)) x11 (.D(and_6_out), .clk(clk), .Q(x11_q), .clr(rst));  // open: en
  Register #(.width(32)) x12 (.D(and_7_out), .clk(clk), .Q(x12_q), .clr(rst));  // open: en
  Register #(.width(32)) x13 (.D(and_8_out), .clk(clk), .Q(x13_q), .clr(rst));  // open: en
  Register #(.width(32)) x14 (.D(and_9_out), .clk(clk), .Q(x14_q), .clr(rst));  // open: en
  Register #(.width(32)) x15 (.D(and_10_out), .clk(clk), .Q(x15_q), .clr(rst));  // open: en
  Multiplexer #(.select(5), .width(32)) multiplexer_1 (
    .in0(x0_q), .in2(x2_q), .in8(x8_q), .in9(x9_q), .in10(x10_q), .in11(x11_q), .in12(x12_q), .in13(x13_q),
    .in14(x14_q), .in15(x15_q), .out(read_data_1), .sel(read_register_1));  // open: in1, in3, in4, in5, in6, in7, in16, in17, in18, in19, in20, in21, in22, in23, in24, in25, in26, in27, in28, in29, in30, in31
  Multiplexer #(.select(5), .width(32)) multiplexer_2 (
    .in0(x0_q), .in2(x2_q), .in8(x8_q), .in9(x9_q), .in10(x10_q), .in11(x11_q), .in12(x12_q), .in13(x13_q),
    .in14(x14_q), .in15(x15_q), .out(read_data_2), .sel(read_register_2));  // open: in1, in3, in4, in5, in6, in7, in16, in17, in18, in19, in20, in21, in22, in23, in24, in25, in26, in27, in28, in29, in30, in31
endmodule

module alu_file (
  input  [31:0] data_1,
  input  [31:0] data_2,
  input  [15:0] inst,
  output [31:0] alu_result
);

  wire [31:0] adder_1_out, multiplexer_1_out, shifter_1_out;

  Adder #(.width(32)) adder_1 (.a(data_1), .b(data_2), .out(adder_1_out));  // open: cin, cout
  Shifter #(.width(32)) shifter_1 (.in(data_1), .\dist (data_2[4:0]), .out(shifter_1_out));
  Multiplexer #(.width(32)) multiplexer_1 (.in0(data_2), .in1(adder_1_out), .out(multiplexer_1_out), .sel(inst[12]));
  Multiplexer #(.select(5), .width(32)) multiplexer_2 (
    .in1(adder_1_out), .in2(shifter_1_out), .in9(data_2), .in13(data_2), .in18(multiplexer_1_out),
    .out(alu_result), .sel({inst[15:13], inst[1:0]}));  // open: in0, in3, in4, in5, in6, in7, in8, in10, in11, in12, in14, in15, in16, in17, in19, in20, in21, in22, in23, in24, in25, in26, in27, in28, in29, in30, in31

  // Notes on the sheet:
  //   rs2/imm
  //   rd/rs1
endmodule

module imm_gen (
  input  [15:0] inst,
  output [31:0] imm
);

  wire [31:0] bit_extender_1_out, shifter_1_out;

  assign bit_extender_1_out = {{26{inst[12]}}, {inst[12], inst[6:2]}};  // Bit_Extender bit_extender_1
  Shifter #(.width(32)) shifter_1 (.in(bit_extender_1_out), .\dist (5'b01100), .out(shifter_1_out));
  Multiplexer #(.select(5), .width(32)) multiplexer_1 (
    .in1(bit_extender_1_out), .in2(bit_extender_1_out), .in9(bit_extender_1_out), .in13(shifter_1_out),
    .out(imm), .sel({inst[15:13], inst[1:0]}));  // open: in0, in3, in4, in5, in6, in7, in8, in10, in11, in12, in14, in15, in16, in17, in18, in19, in20, in21, in22, in23, in24, in25, in26, in27, in28, in29, in30, in31

  // Notes on the sheet:
  //   CI
endmodule

module rs2_or_imm (
  input  [15:0] inst,
  output data_2_choose
);

  Multiplexer #(.select(5)) multiplexer_1 (
    .in1(1'b1), .in2(1'b1), .in9(1'b1), .in13(1'b1), .in18(1'b0), .out(data_2_choose),
    .sel({inst[15:14], inst[2:0]}));  // open: in0, in3, in4, in5, in6, in7, in8, in10, in11, in12, in14, in15, in16, in17, in19, in20, in21, in22, in23, in24, in25, in26, in27, in28, in29, in30, in31
endmodule
